# Fritzing sketch Schematic (saved by Fritzing 0.7.11b)
breadboards: 1

parts:
  Arduino1 = Arduino
  LCD1 = LCD screen
  LCD_Contrast = Rotary Potentiometer (Small) [maximum_resistance=10kΩ]
  Mode = Pushbutton [package="[THT]"]
  Tolerance_Down = Pushbutton [package="[THT]"]
  Tolerance_Up = Pushbutton [package="[THT]"]
  Hall_Effect_3rd_Gear = LM35 Temperature Sensor [package="TO92 [THT]"]
  Hall_Effect_1st_Gear = LM35 Temperature Sensor [package="TO92 [THT]"]
  Hall_Effect_5th_Gear = LM35 Temperature Sensor [package="TO92 [THT]"]
  Hall_Effect_2nd_Gear = LM35 Temperature Sensor [package="TO92 [THT]"]
  Hall_Effect_4th_Gear = LM35 Temperature Sensor [package="TO92 [THT]"]
  Hall_Effect_Reverse = LM35 Temperature Sensor [package="TO92 [THT]"]

nets:
  GND: Arduino1.GND, LCD1.VSS, LCD1.R/W, LCD_Contrast.leg1, Mode.Pin_1, Mode.Pin_2, Tolerance_Down.Pin_1, Tolerance_Down.Pin_2, Tolerance_Up.Pin_1, Tolerance_Up.Pin_2, Hall_Effect_3rd_Gear.GND, Hall_Effect_1st_Gear.GND, Hall_Effect_5th_Gear.GND, Hall_Effect_2nd_Gear.GND, Hall_Effect_4th_Gear.GND, Hall_Effect_Reverse.GND
  N1: Arduino1.D12, LCD1.RS
  N2: Arduino1.D11, LCD1.E
  N3: Arduino1.D10, Tolerance_Down.Pin_3
  N4: Arduino1.D9, Tolerance_Up.Pin_3
  N5: Arduino1.D8, Mode.Pin_3
  N6: Arduino1.D5, LCD1.DB4
  N7: Arduino1.D4, LCD1.DB5
  N8: Arduino1.D3, LCD1.DB6
  N9: Arduino1.D2, LCD1.DB7
  +5V: Arduino1.+5V, LCD1.VDD, LCD_Contrast.leg2, Hall_Effect_3rd_Gear.+Vs, Hall_Effect_1st_Gear.+Vs, Hall_Effect_5th_Gear.+Vs, Hall_Effect_2nd_Gear.+Vs, Hall_Effect_4th_Gear.+Vs, Hall_Effect_Reverse.+Vs
  N10: Arduino1.A0, Hall_Effect_1st_Gear.Vout
  N11: Arduino1.A1, Hall_Effect_2nd_Gear.Vout
  N12: Arduino1.A2, Hall_Effect_3rd_Gear.Vout
  N13: Arduino1.A3, Hall_Effect_4th_Gear.Vout
  N14: Arduino1.A4, Hall_Effect_5th_Gear.Vout
  N15: Arduino1.A5, Hall_Effect_Reverse.Vout
  N16: LCD1.V0, LCD_Contrast.wiper

notes:
  Manual Transmission Shifter Shaft Here (Magnetized)
  Mode
  1st
  2nd
  3rd
  4th
  5th
  Reverse
  Contrast
  Tolerance
  Down
  Tolerance Up
